# Fritzing sketch CWKeyer - Compact (saved by Fritzing 1.0.4)
circuit board: 6.00387cm x 5.7cm
breadboards: 1

parts:
  ESP8266 = NodeMCU V3.0
  R1 = 12mm Trimmer Potentiometer (Large) [maximum_resistance=10kΩ knob_status=50% power=0.5W package=THT]
  Display = male pin header, 4 pins [form="♂ (male)"]
  Encoder = male pin header, 5 pins [form="♂ (male)"]
  Battery = male pin header, 2 pins [form="♂ (male)"]
  Speaker = male pin header, 3 pins [form="♂ (male)"]
  Buzz = Piezo Speaker
  U1 = 3.5mm Audio Jack [package=audio-jack-3.5mm-smd]

nets:
  N1: ESP8266.D0, Encoder.pin4
  N2: ESP8266.D1, Display.pin1
  N3: ESP8266.D2, Display.pin2
  N4: ESP8266.D3, Encoder.pin2
  N5: ESP8266.D4, Encoder.pin3
  N6: ESP8266.3V3, Display.pin3, Encoder.pin5
  N7: ESP8266.GND, R1.leg1, Display.pin4, Encoder.pin1, Battery.pin2, Speaker.pin1, Buzz.pin2, U1.SLEEVE
  N8: ESP8266.D5, R1.leg2
  N9: ESP8266.D6, U1.LEFT
  N10: ESP8266.D7, U1.RIGHT
  N11: ESP8266.D8, Buzz.pin1
  N12: ESP8266.Vin, Battery.pin1
  N13: R1.wiper, Speaker.pin2, Speaker.pin3

notes:
  DL1SKD - CWKeyer - Ver 0.1

custom parts:
  NodeMCU V3.0: ESP8266 based NodeMCU
