# Fritzing sketch CWKeyer (saved by Fritzing 1.0.4)
circuit board: 8.7223cm x 6.03221cm
breadboards: 1

parts:
  Enc = male pin header, 5 pins [form="♂ (male)"]
  Battery = male pin header, 2 pins [form="♂ (male)"]
  Key = male pin header, 3 pins [form="♂ (male)"]
  Spk = male pin header, 3 pins [form="♂ (male)"]
  Display = male pin header, 4 pins [form="♂ (male)"]
  Volume = 6mm Trimmer Potentiometer [maximum_resistance=10kΩ knob_status=50% power=0.5W package=THT]
  J1 = female pin header, 15 pins [form="♀ (female)"]
  J2 = female pin header, 15 pins [form="♀ (female)"]
  C1 = Ceramic Capacitor [capacitance=100nF voltage=35V package="100 mil [THT, multilayer]"]
  R1 = Resistor [tolerance=±5% power=0.25W resistance=10k package=THT]
  R2 = Resistor [tolerance=±5% power=0.25W resistance=10k package=THT]
  In = male pin header, 2 pins [form="♂ (male)"]
  Buzzer = Buzzer 12mm [package=buzzer-12mm]

nets:
  N1: Enc.pin1, Key.pin1, Spk.pin1, Display.pin1, Volume.leg1, J1.pin2, Buzzer.2
  N2: Enc.pin2, J1.pin10
  N3: Enc.pin3, J1.pin15
  N4: Enc.pin4, J1.pin12
  N5: Enc.pin5, J1.pin11
  N6: Battery.pin1, J2.pin15
  N7: Battery.pin2, J2.pin14
  N8: Key.pin2, J1.pin7
  N9: Key.pin3, J1.pin6
  N10: Spk.pin2, Spk.pin3, Volume.wiper
  N11: Display.pin2, J1.pin1
  N12: Display.pin3, J1.pin14
  N13: Display.pin4, J1.pin13
  N14: Volume.leg2, J1.pin8
  N15: J1.pin5, Buzzer.1
  N16: J2.pin1, C1.1, R1.Pin_1, R2.Pin_0
  N17: J2.pin10, R2.Pin_1, In.pin1
  N18: J2.pin11, R1.Pin_0
  N19: C1.0, In.pin2

notes:
  DL1SKD
  CWKeyer
  Ver 0.6
  ESP8266
